// Logisim project BullsAndCows.circ as structural Verilog: 1 circuit, main circuit main
module main (
);

  wire _0_out, _1_out, _2_out, _3_out, _4_out, _5_out, _6_out, _7_out, _8_out, _9_out, button_2_out,
       button_out, Clock, dead, decoder_1_out0, decoder_1_out1, decoder_1_out2, decoder_1_out3, enter,
       invalid, match, random, state_decoder_game, state_decoder_lose, state_decoder_start,
       state_decoder_wait, state_decoder_win;
  wire [1:0] digit_selector_digit_place;
  wire [2:0] state, wins_and_lives_memory_lives;
  wire [3:0] bit_extender_1_out, bulls_with_toggle_and_clear_1_bulls, cows_with_toggle_and_clear_1_cows, D0,
       D1, D2, D3, I0, I1, I2, I3, S0, S1, S2, S3, T0, T1, T2, T3, wins_and_lives_memory_wins;
  wire [15:0] random_rand_output;

  Button _2 (.out(_2_out));
  Button _1 (.out(_1_out));
  Button _5 (.out(_5_out));
  Button _4 (.out(_4_out));
  Button _8 (.out(_8_out));
  Button _7 (.out(_7_out));
  Button R (.out(random));
  Button _0 (.out(_0_out));
  Button button (.out(button_out));
  Button u_Enter (.out(enter));
  Button _3 (.out(_3_out));
  Button _6 (.out(_6_out));
  Button _9 (.out(_9_out));
  digit_selector digit_selector (
    .L(button_out), .R(button_2_out), .clock(Clock), .state(state), .Digit_Place(digit_selector_digit_place));
  Button button_2 (.out(button_2_out));
  Random_generator u_random (.random_button(random), .clock(Clock), .state(state), .Rand_output(random_rand_output));
  Digit_input_with_random_input digit_input_with_random_input_1 (
    ._0(_0_out), ._1(_1_out), ._2(_2_out), ._3(_3_out), ._4(_4_out), ._5(_5_out), ._6(_6_out), ._7(_7_out),
    ._8(_8_out), ._9(_9_out), .random_input(random_rand_output), .random_click(random), .clock(Clock),
    .in_14(digit_selector_digit_place), .State(state), .I0(I0), .I1(I1), .I2(I2), .I3(I3));
  Hex_Digit_Display hex_digit_display_1 (.value(wins_and_lives_memory_wins));  // open: dp
  win_lives_memory_with_samedigit_detector wins_and_lives_memory (
    .match(match), .error(invalid), .state(state), .clock(Clock), .wins(wins_and_lives_memory_wins),
    .lives(wins_and_lives_memory_lives));
  Hex_Digit_Display hex_digit_display_2 (.value(bit_extender_1_out));  // open: dp
  assign bit_extender_1_out = {{1{1'b0}}, wins_and_lives_memory_lives};  // Bit_Extender bit_extender_1
  Clock clock_1 (.out(Clock));
  and and_1 (dead, wins_and_lives_memory_lives[0], ~wins_and_lives_memory_lives[1], ~wins_and_lives_memory_lives[2]);  // AND_Gate
  store_memory_with_samedigit__detector setup_digits_memory (
    .I0(I0), .I1(I1), .I2(I2), .I3(I3), .Enter(enter), .Error(invalid), .state(state), .clock(Clock),
    .s0(S0), .s1(S1), .s2(S2), .s3(S3));
  try_memory_with_reset try_memory_with_reset_1 (
    .I0(I0), .I1(I1), .I2(I2), .I3(I3), .Enter(enter), .Error(invalid), .state(state), .clock(Clock),
    .s0(T0), .s1(T1), .s2(T2), .s3(T3));
  // Probe on state
  Circuit_Controller_w__Error_Check next_state_controller (
    .error(invalid), .zerolives(dead), .win(match), .enter(enter), .Clock(Clock), .Output(state));
  Decoder #(.select(2)) decoder_1 (
    .out0(decoder_1_out0), .out1(decoder_1_out1), .out2(decoder_1_out2), .out3(decoder_1_out3),
    .sel(digit_selector_digit_place));  // open: en
  LED led_1 (.in(decoder_1_out3));
  Hex_Digit_Display hex_digit_display_3 (.value(D3));  // open: dp
  LED led_2 (.in(decoder_1_out2));
  LED led_3 (.in(decoder_1_out1));
  Hex_Digit_Display hex_digit_display_4 (.value(D1));  // open: dp
  Hex_Digit_Display hex_digit_display_5 (.value(D2));  // open: dp
  LED led_4 (.in(decoder_1_out0));
  Hex_Digit_Display hex_digit_display_6 (.value(D0));  // open: dp
  digit_display digit_display_picker (
    .I0(I0), .I1(I1), .I2(I2), .I3(I3), .S0(S0), .S1(S1), .S2(S2), .S3(S3), .state(state), .D0(D0), .D1(D1),
    .D2(D2), .D3(D3));
  LED led_5 (.in(invalid));
  Hex_Digit_Display hex_digit_display_7 (.value(S3));  // open: dp
  same_digit error_check (.t1(I0), .t2(I1), .t3(I2), .t4(I3), .state(state), .same_digit(invalid));
  bulls_with_toggle_and_clear bulls_with_toggle_and_clear_1 (
    .tr1(T0), .tr2(T1), .tr3(T2), .tr4(T3), .sr1(S0), .sr2(S1), .sr3(S2), .sr4(S3), .state(state),
    .Bulls(bulls_with_toggle_and_clear_1_bulls), .match(match));
  cows_with_toggle_and_clear cows_with_toggle_and_clear_1 (
    .tr1(T0), .tr2(T1), .tr3(T2), .tr4(T3), .sr1(S0), .sr2(S1), .sr3(S2), .sr4(S3), .state(state),
    .Cows(cows_with_toggle_and_clear_1_cows));
  Hex_Digit_Display hex_digit_display_8 (.value(S1));  // open: dp
  Hex_Digit_Display hex_digit_display_9 (.value(S2));  // open: dp
  LED start (.in(state_decoder_start));
  state_to_led_decoder state_decoder (
    .start(state_decoder_start), .game(state_decoder_game), .\wait (state_decoder_wait),
    .win(state_decoder_win), .lose(state_decoder_lose), .state(state), .match(match));
  Hex_Digit_Display hex_digit_display_10 (.value(S0));  // open: dp
  LED game (.in(state_decoder_game));
  LED \wait  (.in(state_decoder_wait));
  LED lose (.in(state_decoder_lose));
  LED win (.in(state_decoder_win));
  Hex_Digit_Display hex_digit_display_11 (.value(cows_with_toggle_and_clear_1_cows));  // open: dp
  Hex_Digit_Display hex_digit_display_12 (.value(bulls_with_toggle_and_clear_1_bulls));  // open: dp

  // Notes on the sheet:
  //   Input Buttons
  //   Wins
  //   Lives
  //   Input Display Digits
  //   ERROR
  //   Saved Setup Digits
  //   Bulls
  //   Cows
endmodule
